// Logisim project T8.circ as structural Verilog: 6 circuits, main circuit main
module main (
  input  in_1,
  input  in_2,
  input  [7:0] in_3,
  output [15:0] out_4,
  output [7:0] out_5
);

  wire and_1_out, and_2_out, and_3_out, and_4_out, and_5_out, and_6_out, and_7_out, and_8_out, and_9_out,
       clk_divader_1_out_3, clk_divader_1_out_4, clock_1_out, decoder_1_out0, decoder_1_out1, decoder_1_out2,
       decoder_1_out3, decoder_2_out1, decoder_2_out2, not_1_out;

  not not_1 (not_1_out, decoder_2_out1);
  and and_1 (and_1_out, in_2, not_1_out);
  Decoder #(.select(2), .enable("false")) decoder_1 (
    .out0(decoder_1_out0), .out1(decoder_1_out1), .out2(decoder_1_out2), .out3(decoder_1_out3),
    .sel({out_4[12], out_4[13]}));
  Clock clock_1 (.out(clock_1_out));
  Decoder #(.select(2), .enable("false")) decoder_2 (
    .out1(decoder_2_out1), .out2(decoder_2_out2), .sel({out_4[14], out_4[15]}));  // open: out0, out3
  and and_2 (and_2_out, decoder_2_out1, decoder_1_out0);
  and and_3 (and_3_out, decoder_2_out2, decoder_1_out0);
  and and_4 (and_4_out, decoder_2_out1, decoder_1_out1);
  and and_5 (and_5_out, decoder_2_out2, decoder_1_out1);
  and and_6 (and_6_out, decoder_2_out1, decoder_1_out2);
  and and_7 (and_7_out, decoder_2_out2, decoder_1_out2);
  and and_8 (and_8_out, decoder_2_out1, decoder_1_out3);
  and and_9 (and_9_out, decoder_2_out2, decoder_1_out3);
  CLK_Divader clk_divader_1 (.out_3(clk_divader_1_out_3), .in_1(clock_1_out), .in_2(in_1), .out_4(clk_divader_1_out_4));
  RAM ram_1 (.addr(out_4[11:4]), .we(decoder_2_out2), .oe(decoder_2_out1), .clk(clock_1_out), .data(out_5));
  Instructuon_Register instructuon_register_1 (
    .INST_IN(in_3), .WRT(clk_divader_1_out_4), .CLK(clock_1_out), .RST(in_1), .READ(clk_divader_1_out_3),
    .INST_OUT(out_4));
  Ram_Adress_Register ram_adress_register_1 (
    .CLK(clock_1_out), .RST(in_1), .ADRESS_OUT(out_4[11:4]));  // open: ADRESS_IN, WRT, READ
  LED led_1 (.in(out_5[7]));
  Program_Counter program_counter_1 (
    .RST(in_1), .EN(and_1_out), .CLK(clock_1_out), .ADRESS_OUT(out_5));  // open: JUMP, ADRESS_IN
  Rx_Register rx_register_1 (
    .DATA_IN(out_5), .WRT(and_2_out), .CLK(clock_1_out), .RST(in_1), .READ(and_3_out), .DATA_OUT(out_5));
  Rx_Register rx_register_2 (
    .DATA_IN(out_5), .WRT(and_4_out), .CLK(clock_1_out), .RST(in_1), .READ(and_5_out), .DATA_OUT(out_5));
  Rx_Register rx_register_3 (
    .DATA_IN(out_5), .WRT(and_6_out), .CLK(clock_1_out), .RST(in_1), .READ(and_7_out), .DATA_OUT(out_5));
  Rx_Register rx_register_4 (
    .DATA_IN(out_5), .WRT(and_8_out), .CLK(clock_1_out), .RST(in_1), .READ(and_9_out), .DATA_OUT(out_5));
  LED led_2 (.in(out_5[6]));
  LED led_3 (.in(out_5[4]));
  LED led_4 (.in(out_5[5]));
  LED led_5 (.in(out_5[3]));
  Pull_Resistor pull_resistor_1 (.node(out_5[4]));
  Pull_Resistor pull_resistor_2 (.node(out_5[7]));
  Pull_Resistor pull_resistor_3 (.node(out_5[3]));
  Pull_Resistor pull_resistor_4 (.node(out_5[5]));
  Pull_Resistor pull_resistor_5 (.node(out_5[6]));
  LED led_6 (.in(out_5[0]));
  LED led_7 (.in(out_5[1]));
  LED led_8 (.in(out_5[2]));
  Pull_Resistor pull_resistor_6 (.node(out_5[0]));
  Pull_Resistor pull_resistor_7 (.node(out_5[2]));
  Pull_Resistor pull_resistor_8 (.node(out_5[1]));
endmodule

module Program_Counter (
  input  RST,
  input  JUMP,
  input  EN,
  input  CLK,
  input  [7:0] ADRESS_IN,
  output [7:0] ADRESS_OUT
);

  wire [7:0] counter_1_q;

  Counter counter_1 (
    .clr(RST), .load(JUMP), .up(1'b1), .count(EN), .clk(CLK), .D(ADRESS_IN), .Q(counter_1_q));  // open: carry
  assign ADRESS_OUT = EN ? counter_1_q : 8'bz;  // Controlled_Buffer controlled_buffer_1
endmodule

module Ram_Adress_Register (
  input  [7:0] ADRESS_IN,
  input  WRT,
  input  CLK,
  input  RST,
  input  READ,
  output [7:0] ADRESS_OUT
);

  wire [7:0] register_1_q;

  Register register_1 (.D(ADRESS_IN), .en(WRT), .clk(CLK), .Q(register_1_q), .clr(RST));
  assign ADRESS_OUT = READ ? register_1_q : 8'bz;  // Controlled_Buffer controlled_buffer_1
endmodule

module Rx_Register (
  input  [7:0] DATA_IN,
  input  WRT,
  input  CLK,
  input  RST,
  input  READ,
  output [7:0] DATA_OUT
);

  wire [7:0] register_1_q;

  Register register_1 (.D(DATA_IN), .en(WRT), .clk(CLK), .Q(register_1_q), .clr(RST));
  assign DATA_OUT = READ ? register_1_q : 8'bz;  // Controlled_Buffer controlled_buffer_1
endmodule

module Instructuon_Register (
  input  [7:0] INST_IN,
  input  WRT,
  input  CLK,
  input  RST,
  input  READ,
  output [15:0] INST_OUT
);

  wire not_1_out;
  wire [7:0] register_1_q, register_2_q;

  Register register_1 (.D(INST_IN), .en(WRT), .clk(CLK), .Q(register_1_q), .clr(RST));
  Register register_2 (.D(register_1_q), .en(WRT), .clk(CLK), .Q(register_2_q), .clr(RST));
  assign INST_OUT = READ ? {register_2_q, register_1_q} : 16'bz;  // Controlled_Buffer controlled_buffer_1
  not not_1 (not_1_out, READ);
  assign INST_OUT = not_1_out ? {16{1'b0}} : 16'bz;  // Controlled_Buffer controlled_buffer_2
endmodule

module CLK_Divader (
  input  in_1,
  input  in_2,
  output out_3,
  output out_4
);

  wire t_ff_1_q;

  T_Flip_Flop t_ff_1 (.T(1'b1), .clk(in_1), .Q(t_ff_1_q), .reset(in_2));  // open: Qn, preset
  T_Flip_Flop t_ff_2 (.T(t_ff_1_q), .clk(in_1), .Q(out_3), .reset(in_2));  // open: Qn, preset
  not not_1 (out_4, out_3);
endmodule
